// Logisim project CPU-halime-13.05.circ as structural Verilog
module ALU (
  input  [31:0] A,
  input  [31:0] B,
  input  [3:0] in_3,
  input  [4:0] shift_amount,
  output [31:0] ALU_OUT,
  output zero_flag
);

  wire [31:0] adder_1_out, and_1_out, negator_1_out, not_1_out, or_1_out, shifter_1_out, shifter_2_out,
       subtractor_1_out, xor_1_out;

  assign and_1_out = B & A;  // AND_Gate and_1, 32 bits wide
  assign or_1_out = B | A;  // OR_Gate or_1, 32 bits wide
  assign xor_1_out = B ^ A;  // XOR_Gate xor_1, 32 bits wide
  assign not_1_out = ~A;  // NOT_Gate not_1, 32 bits wide
  Adder #(.width(32)) adder_1 (.a(A), .b(B), .out(adder_1_out));  // open: cin, cout
  Subtractor #(.width(32)) subtractor_1 (.a(A), .b(B), .out(subtractor_1_out));  // open: bin, bout
  Negator #(.width(32)) negator_1 (.in(A), .out(negator_1_out));
  Shifter #(.width(32)) shifter_1 (.in(A), .\dist (shift_amount), .out(shifter_1_out));
  Shifter #(.width(32), .shift("lr")) shifter_2 (.in(A), .\dist (shift_amount), .out(shifter_2_out));
  Multiplexer #(.select(4), .width(32)) multiplexer_1 (
    .in0(and_1_out), .in1(or_1_out), .in2(xor_1_out), .in3(not_1_out), .in4(adder_1_out),
    .in5(subtractor_1_out), .in6(negator_1_out), .in7(shifter_1_out), .in8(shifter_2_out), .out(ALU_OUT),
    .sel(in_3));  // open: in9, in10, in11, in12, in13, in14, in15, en
  Comparator #(.width(32)) comparator_1 (.a(ALU_OUT), .b({32{1'b0}}), .eq(zero_flag));  // open: gt, lt

  // Notes on the sheet:
  //   A+B
  //   A-B
  //   -A
  //   logic left
  //   logic right
endmodule

module Registers (
  input  [31:0] BusW,
  input  RegWr,
  input  clock,
  input  [4:0] RW,
  input  [4:0] RA_Rs,
  input  [4:0] RB_Rt,
  output [31:0] BusA,
  output [31:0] BusB
);

  wire demultiplexer_1_out0, demultiplexer_1_out1, demultiplexer_1_out2, demultiplexer_1_out3,
       demultiplexer_1_out4, demultiplexer_1_out5, demultiplexer_1_out6, demultiplexer_1_out7,
       demultiplexer_1_out8, demultiplexer_1_out9, demultiplexer_1_out10, demultiplexer_1_out11,
       demultiplexer_1_out12, demultiplexer_1_out13, demultiplexer_1_out14, demultiplexer_1_out15,
       demultiplexer_1_out16, demultiplexer_1_out17, demultiplexer_1_out18, demultiplexer_1_out19,
       demultiplexer_1_out20, demultiplexer_1_out21, demultiplexer_1_out22, demultiplexer_1_out23,
       demultiplexer_1_out24, demultiplexer_1_out25, demultiplexer_1_out26, demultiplexer_1_out27,
       demultiplexer_1_out28, demultiplexer_1_out29, demultiplexer_1_out30, demultiplexer_1_out31;
  wire [31:0] R0_q, R1_q, R2_q, R3_q, R4_q, R5_q, R6_q, R7_q, R8_q, R9_q, R10_q, R11_q, R12_q, R13_q, R14_q,
       R15_q, R16_q, R17_q, R18_q, R19_q, R20_q, R21_q, R22_q, R23_q, R24_q, R25_q, R26_q, R27_q, R28_q,
       R29_q, R30_q, R31_q;

  Demultiplexer #(.select(5)) demultiplexer_1 (
    .out0(demultiplexer_1_out0), .out1(demultiplexer_1_out1), .out2(demultiplexer_1_out2),
    .out3(demultiplexer_1_out3), .out4(demultiplexer_1_out4), .out5(demultiplexer_1_out5),
    .out6(demultiplexer_1_out6), .out7(demultiplexer_1_out7), .out8(demultiplexer_1_out8),
    .out9(demultiplexer_1_out9), .out10(demultiplexer_1_out10), .out11(demultiplexer_1_out11),
    .out12(demultiplexer_1_out12), .out13(demultiplexer_1_out13), .out14(demultiplexer_1_out14),
    .out15(demultiplexer_1_out15), .out16(demultiplexer_1_out16), .out17(demultiplexer_1_out17),
    .out18(demultiplexer_1_out18), .out19(demultiplexer_1_out19), .out20(demultiplexer_1_out20),
    .out21(demultiplexer_1_out21), .out22(demultiplexer_1_out22), .out23(demultiplexer_1_out23),
    .out24(demultiplexer_1_out24), .out25(demultiplexer_1_out25), .out26(demultiplexer_1_out26),
    .out27(demultiplexer_1_out27), .out28(demultiplexer_1_out28), .out29(demultiplexer_1_out29),
    .out30(demultiplexer_1_out30), .out31(demultiplexer_1_out31), .in(clock), .sel(RW), .en(RegWr));
  Register #(.width(32)) R31 (.D(BusW), .Q(R31_q), .clk(demultiplexer_1_out31));  // open: en, clr
  Register #(.width(32)) R29 (.D(BusW), .Q(R29_q), .clk(demultiplexer_1_out29));  // open: en, clr
  Register #(.width(32)) R27 (.D(BusW), .Q(R27_q), .clk(demultiplexer_1_out27));  // open: en, clr
  Register #(.width(32)) R25 (.D(BusW), .Q(R25_q), .clk(demultiplexer_1_out25));  // open: en, clr
  Register #(.width(32)) R23 (.D(BusW), .Q(R23_q), .clk(demultiplexer_1_out23));  // open: en, clr
  Register #(.width(32)) R21 (.D(BusW), .Q(R21_q), .clk(demultiplexer_1_out21));  // open: en, clr
  Register #(.width(32)) R19 (.D(BusW), .Q(R19_q), .clk(demultiplexer_1_out19));  // open: en, clr
  Register #(.width(32)) R17 (.D(BusW), .Q(R17_q), .clk(demultiplexer_1_out17));  // open: en, clr
  Register #(.width(32)) R15 (.D(BusW), .Q(R15_q), .clk(demultiplexer_1_out15));  // open: en, clr
  Register #(.width(32)) R13 (.D(BusW), .Q(R13_q), .clk(demultiplexer_1_out13));  // open: en, clr
  Register #(.width(32)) R11 (.D(BusW), .Q(R11_q), .clk(demultiplexer_1_out11));  // open: en, clr
  Register #(.width(32)) R9 (.D(BusW), .Q(R9_q), .clk(demultiplexer_1_out9));  // open: en, clr
  Register #(.width(32)) R7 (.D(BusW), .Q(R7_q), .clk(demultiplexer_1_out7));  // open: en, clr
  Register #(.width(32)) R5 (.D(BusW), .Q(R5_q), .clk(demultiplexer_1_out5));  // open: en, clr
  Register #(.width(32)) R3 (.D(BusW), .Q(R3_q), .clk(demultiplexer_1_out3));  // open: en, clr
  Register #(.width(32)) R1 (.D(BusW), .Q(R1_q), .clk(demultiplexer_1_out1));  // open: en, clr
  Register #(.width(32)) R30 (.D(BusW), .Q(R30_q), .clk(demultiplexer_1_out30));  // open: en, clr
  Register #(.width(32)) R28 (.D(BusW), .Q(R28_q), .clk(demultiplexer_1_out28));  // open: en, clr
  Register #(.width(32)) R26 (.D(BusW), .Q(R26_q), .clk(demultiplexer_1_out26));  // open: en, clr
  Register #(.width(32)) R24 (.D(BusW), .Q(R24_q), .clk(demultiplexer_1_out24));  // open: en, clr
  Register #(.width(32)) R22 (.D(BusW), .Q(R22_q), .clk(demultiplexer_1_out22));  // open: en, clr
  Register #(.width(32)) R20 (.D(BusW), .Q(R20_q), .clk(demultiplexer_1_out20));  // open: en, clr
  Register #(.width(32)) R18 (.D(BusW), .Q(R18_q), .clk(demultiplexer_1_out18));  // open: en, clr
  Register #(.width(32)) R16 (.D(BusW), .Q(R16_q), .clk(demultiplexer_1_out16));  // open: en, clr
  Register #(.width(32)) R14 (.D(BusW), .Q(R14_q), .clk(demultiplexer_1_out14));  // open: en, clr
  Register #(.width(32)) R12 (.D(BusW), .Q(R12_q), .clk(demultiplexer_1_out12));  // open: en, clr
  Register #(.width(32)) R10 (.D(BusW), .Q(R10_q), .clk(demultiplexer_1_out10));  // open: en, clr
  Register #(.width(32)) R8 (.D(BusW), .Q(R8_q), .clk(demultiplexer_1_out8));  // open: en, clr
  Register #(.width(32)) R6 (.D(BusW), .Q(R6_q), .clk(demultiplexer_1_out6));  // open: en, clr
  Register #(.width(32)) R4 (.D(BusW), .Q(R4_q), .clk(demultiplexer_1_out4));  // open: en, clr
  Register #(.width(32)) R2 (.D(BusW), .Q(R2_q), .clk(demultiplexer_1_out2));  // open: en, clr
  Register #(.width(32)) R0 (.D({32{1'b0}}), .Q(R0_q), .clk(demultiplexer_1_out0));  // open: en, clr
  Multiplexer #(.select(5), .width(32)) multiplexer_1 (
    .in0(R0_q), .in1(R1_q), .in2(R2_q), .in3(R3_q), .in4(R4_q), .in5(R5_q), .in6(R6_q), .in7(R7_q),
    .in8(R8_q), .in9(R9_q), .in10(R10_q), .in11(R11_q), .in12(R12_q), .in13(R13_q), .in14(R14_q),
    .in15(R15_q), .in16(R16_q), .in17(R17_q), .in18(R18_q), .in19(R19_q), .in20(R20_q), .in21(R21_q),
    .in22(R22_q), .in23(R23_q), .in24(R24_q), .in25(R25_q), .in26(R26_q), .in27(R27_q), .in28(R28_q),
    .in29(R29_q), .in30(R30_q), .in31(R31_q), .out(BusA), .sel(RA_Rs));  // open: en
  Multiplexer #(.select(5), .width(32)) multiplexer_2 (
    .in0(R0_q), .in1(R1_q), .in2(R2_q), .in3(R3_q), .in4(R4_q), .in5(R5_q), .in6(R6_q), .in7(R7_q),
    .in8(R8_q), .in9(R9_q), .in10(R10_q), .in11(R11_q), .in12(R12_q), .in13(R13_q), .in14(R14_q),
    .in15(R15_q), .in16(R16_q), .in17(R17_q), .in18(R18_q), .in19(R19_q), .in20(R20_q), .in21(R21_q),
    .in22(R22_q), .in23(R23_q), .in24(R24_q), .in25(R25_q), .in26(R26_q), .in27(R27_q), .in28(R28_q),
    .in29(R29_q), .in30(R30_q), .in31(R31_q), .out(BusB), .sel(RB_Rt));  // open: en

  // Notes on the sheet:
  //   RegWr girişini gözden geçir. Doğru yere mi bağladım bilmiyorum????
endmodule

module halime (
);

  wire undriven, undriven_2;
  wire [3:0] undriven_3;
  wire [4:0] inst_q_2, multiplexer_1_out;
  wire [31:0] A_q, B_q, bit_extender_1_out, inst_q, multiplexer_2_out, part_1_branch_target_address,
       registers_1_busa, registers_1_busb, rom_1_data;

  Register #(.width(32)) inst (.D(rom_1_data), .Q({inst_q[31:26], inst_q_2, inst_q[20:0]}));  // open: en, clk, clr
  ROM #(.addrWidth(5), .dataWidth(32)) rom_1 (.data(rom_1_data));  // open: addr, sel
  assign bit_extender_1_out = {{16{inst_q[31]}}, {inst_q[31:26], inst_q_2, inst_q[20:16]}};  // Bit_Extender bit_extender_1
  Multiplexer #(.width(5)) multiplexer_1 (
    .in0(inst_q[15:11]), .in1(inst_q[20:16]), .out(multiplexer_1_out), .sel(undriven));  // open: en
  circuit part_1 (
    .imm32(bit_extender_1_out), .Branch_Target_Address(part_1_branch_target_address));  // open: next_pc_address
  Registers registers_1 (
    .RB_Rt(inst_q[15:11]), .BusA(registers_1_busa), .RA_Rs(inst_q[10:6]), .BusB(registers_1_busb));  // open: RW, BusW, RegWr, clock
  Register #(.width(32)) BTA (.D(part_1_branch_target_address));  // open: en, Q, clk, clr
  Register #(.width(32)) Imm (.D(bit_extender_1_out));  // open: en, Q, clk, clr
  Register #(.width(32)) A (.D(registers_1_busa), .Q(A_q));  // open: en, clk, clr
  Register #(.width(32)) B (.D(registers_1_busb), .Q(B_q));  // open: en, clk, clr
  Register #(.width(5)) Rd2 (.D(multiplexer_1_out));  // open: en, Q, clk, clr
  Multiplexer #(.width(32)) multiplexer_2 (
    .in0(B_q), .in1(A_q), .out(multiplexer_2_out), .sel(undriven_2));  // open: en
  ALU alu_1 (.A(A_q), .B(multiplexer_2_out), .in_3(undriven_3), .shift_amount(inst_q_2));  // open: ALU_OUT, zero_flag

  // Notes on the sheet:
  //   imm
  //   opcode
  //   sa
  //   func
  //   rs
  //   rt
  //   rd
endmodule

module circuit (
  input  [31:0] next_pc_address,
  input  [31:0] imm32,
  output [31:0] Branch_Target_Address
);

  wire [31:0] shifter_1_out;

  Shifter #(.width(32)) shifter_1 (.in(imm32), .\dist (5'b00010), .out(shifter_1_out));
  Adder #(.width(32)) adder_1 (.a(next_pc_address), .b(shifter_1_out), .out(Branch_Target_Address));  // open: cin, cout
endmodule
