// Logisim project CPU.circ as structural Verilog: 9 circuits, main circuit main
module ALU (
  input  [31:0] A,
  input  [31:0] B,
  input  [3:0] in_3,
  input  [4:0] shift_amount,
  output [31:0] ALU_OUT,
  output zero_flag
);

  wire [31:0] adder_1_out, and_1_out, negator_1_out, not_1_out, or_1_out, shifter_1_out, shifter_2_out,
       subtractor_1_out, xor_1_out;

  assign and_1_out = B & A;  // AND_Gate and_1, 32 bits wide
  assign or_1_out = B | A;  // OR_Gate or_1, 32 bits wide
  assign xor_1_out = B ^ A;  // XOR_Gate xor_1, 32 bits wide
  assign not_1_out = ~A;  // NOT_Gate not_1, 32 bits wide
  Adder #(.width(32)) adder_1 (.a(A), .b(B), .out(adder_1_out));  // open: cin, cout
  Subtractor #(.width(32)) subtractor_1 (.a(A), .b(B), .out(subtractor_1_out));  // open: bin, bout
  Negator #(.width(32)) negator_1 (.in(A), .out(negator_1_out));
  Shifter #(.width(32)) shifter_1 (.in(B), .\dist (shift_amount), .out(shifter_1_out));
  Shifter #(.width(32), .shift("lr")) shifter_2 (.in(A), .\dist (shift_amount), .out(shifter_2_out));
  Multiplexer #(.select(4), .width(32)) multiplexer_1 (
    .in0(and_1_out), .in1(or_1_out), .in2(xor_1_out), .in3(not_1_out), .in4(adder_1_out),
    .in5(subtractor_1_out), .in6(negator_1_out), .in7(shifter_1_out), .in8(shifter_2_out), .out(ALU_OUT),
    .sel(in_3));  // open: in9, in10, in11, in12, in13, in14, in15, en
  Comparator #(.width(32)) comparator_1 (.a(ALU_OUT), .b({32{1'b0}}), .eq(zero_flag));  // open: gt, lt

  // Notes on the sheet:
  //   A+B
  //   A-B
  //   -A
  //   logic left
  //   logic right
endmodule

module Registers (
  input  [31:0] BusW,
  input  RegWr,
  input  clock,
  input  [4:0] RW,
  input  [4:0] RA_Rs,
  input  [4:0] RB_Rt,
  output [31:0] BusA,
  output [31:0] BusB,
  output [31:0] a1
);

  wire demultiplexer_1_out0, demultiplexer_1_out1, demultiplexer_1_out2, demultiplexer_1_out3,
       demultiplexer_1_out4, demultiplexer_1_out5, demultiplexer_1_out6, demultiplexer_1_out7,
       demultiplexer_1_out8, demultiplexer_1_out9, demultiplexer_1_out10, demultiplexer_1_out11,
       demultiplexer_1_out12, demultiplexer_1_out13, demultiplexer_1_out14, demultiplexer_1_out15,
       demultiplexer_1_out16, demultiplexer_1_out17, demultiplexer_1_out18, demultiplexer_1_out19,
       demultiplexer_1_out20, demultiplexer_1_out21, demultiplexer_1_out22, demultiplexer_1_out23,
       demultiplexer_1_out24, demultiplexer_1_out25, demultiplexer_1_out26, demultiplexer_1_out27,
       demultiplexer_1_out28, demultiplexer_1_out29, demultiplexer_1_out30, demultiplexer_1_out31;
  wire [31:0] R0_q, R1_q, R2_q, R3_q, R4_q, R6_q, R7_q, R8_q, R9_q, R10_q, R11_q, R12_q, R13_q, R14_q, R15_q,
       R16_q, R17_q, R18_q, R19_q, R20_q, R21_q, R22_q, R23_q, R24_q, R25_q, R26_q, R27_q, R28_q, R29_q,
       R30_q, R31_q;

  Demultiplexer #(.select(5)) demultiplexer_1 (
    .out0(demultiplexer_1_out0), .out1(demultiplexer_1_out1), .out2(demultiplexer_1_out2),
    .out3(demultiplexer_1_out3), .out4(demultiplexer_1_out4), .out5(demultiplexer_1_out5),
    .out6(demultiplexer_1_out6), .out7(demultiplexer_1_out7), .out8(demultiplexer_1_out8),
    .out9(demultiplexer_1_out9), .out10(demultiplexer_1_out10), .out11(demultiplexer_1_out11),
    .out12(demultiplexer_1_out12), .out13(demultiplexer_1_out13), .out14(demultiplexer_1_out14),
    .out15(demultiplexer_1_out15), .out16(demultiplexer_1_out16), .out17(demultiplexer_1_out17),
    .out18(demultiplexer_1_out18), .out19(demultiplexer_1_out19), .out20(demultiplexer_1_out20),
    .out21(demultiplexer_1_out21), .out22(demultiplexer_1_out22), .out23(demultiplexer_1_out23),
    .out24(demultiplexer_1_out24), .out25(demultiplexer_1_out25), .out26(demultiplexer_1_out26),
    .out27(demultiplexer_1_out27), .out28(demultiplexer_1_out28), .out29(demultiplexer_1_out29),
    .out30(demultiplexer_1_out30), .out31(demultiplexer_1_out31), .in(clock), .sel(RW), .en(RegWr));
  Register #(.width(32)) R31 (.D(BusW), .Q(R31_q), .clk(demultiplexer_1_out31));  // open: en, clr
  Register #(.width(32)) R29 (.D(BusW), .Q(R29_q), .clk(demultiplexer_1_out29));  // open: en, clr
  Register #(.width(32)) R27 (.D(BusW), .Q(R27_q), .clk(demultiplexer_1_out27));  // open: en, clr
  Register #(.width(32)) R25 (.D(BusW), .Q(R25_q), .clk(demultiplexer_1_out25));  // open: en, clr
  Register #(.width(32)) R23 (.D(BusW), .Q(R23_q), .clk(demultiplexer_1_out23));  // open: en, clr
  Register #(.width(32)) R21 (.D(BusW), .Q(R21_q), .clk(demultiplexer_1_out21));  // open: en, clr
  Register #(.width(32)) R19 (.D(BusW), .Q(R19_q), .clk(demultiplexer_1_out19));  // open: en, clr
  Register #(.width(32)) R17 (.D(BusW), .Q(R17_q), .clk(demultiplexer_1_out17));  // open: en, clr
  Register #(.width(32)) R15 (.D(BusW), .Q(R15_q), .clk(demultiplexer_1_out15));  // open: en, clr
  Register #(.width(32)) R13 (.D(BusW), .Q(R13_q), .clk(demultiplexer_1_out13));  // open: en, clr
  Register #(.width(32)) R11 (.D(BusW), .Q(R11_q), .clk(demultiplexer_1_out11));  // open: en, clr
  Register #(.width(32)) R9 (.D(BusW), .Q(R9_q), .clk(demultiplexer_1_out9));  // open: en, clr
  Register #(.width(32)) R7 (.D(BusW), .Q(R7_q), .clk(demultiplexer_1_out7));  // open: en, clr
  Register #(.width(32)) R5 (.D(BusW), .Q(a1), .clk(demultiplexer_1_out5));  // open: en, clr
  Register #(.width(32)) R3 (.D(BusW), .Q(R3_q), .clk(demultiplexer_1_out3));  // open: en, clr
  Register #(.width(32)) R1 (.D(BusW), .Q(R1_q), .clk(demultiplexer_1_out1));  // open: en, clr
  Register #(.width(32)) R30 (.D(BusW), .Q(R30_q), .clk(demultiplexer_1_out30));  // open: en, clr
  Register #(.width(32)) R28 (.D(BusW), .Q(R28_q), .clk(demultiplexer_1_out28));  // open: en, clr
  Register #(.width(32)) R26 (.D(BusW), .Q(R26_q), .clk(demultiplexer_1_out26));  // open: en, clr
  Register #(.width(32)) R24 (.D(BusW), .Q(R24_q), .clk(demultiplexer_1_out24));  // open: en, clr
  Register #(.width(32)) R22 (.D(BusW), .Q(R22_q), .clk(demultiplexer_1_out22));  // open: en, clr
  Register #(.width(32)) R20 (.D(BusW), .Q(R20_q), .clk(demultiplexer_1_out20));  // open: en, clr
  Register #(.width(32)) R18 (.D(BusW), .Q(R18_q), .clk(demultiplexer_1_out18));  // open: en, clr
  Register #(.width(32)) R16 (.D(BusW), .Q(R16_q), .clk(demultiplexer_1_out16));  // open: en, clr
  Register #(.width(32)) R14 (.D(BusW), .Q(R14_q), .clk(demultiplexer_1_out14));  // open: en, clr
  Register #(.width(32)) R12 (.D(BusW), .Q(R12_q), .clk(demultiplexer_1_out12));  // open: en, clr
  Register #(.width(32)) R10 (.D(BusW), .Q(R10_q), .clk(demultiplexer_1_out10));  // open: en, clr
  Register #(.width(32)) R8 (.D(BusW), .Q(R8_q), .clk(demultiplexer_1_out8));  // open: en, clr
  Register #(.width(32)) R6 (.D(BusW), .Q(R6_q), .clk(demultiplexer_1_out6));  // open: en, clr
  Register #(.width(32)) R4 (.D(BusW), .Q(R4_q), .clk(demultiplexer_1_out4));  // open: en, clr
  Register #(.width(32)) R2 (.D(BusW), .Q(R2_q), .clk(demultiplexer_1_out2));  // open: en, clr
  Register #(.width(32)) R0 (.D({32{1'b0}}), .Q(R0_q), .clk(demultiplexer_1_out0));  // open: en, clr
  Multiplexer #(.select(5), .width(32)) multiplexer_1 (
    .in0(R0_q), .in1(R1_q), .in2(R2_q), .in3(R3_q), .in4(R4_q), .in5(a1), .in6(R6_q), .in7(R7_q), .in8(R8_q),
    .in9(R9_q), .in10(R10_q), .in11(R11_q), .in12(R12_q), .in13(R13_q), .in14(R14_q), .in15(R15_q),
    .in16(R16_q), .in17(R17_q), .in18(R18_q), .in19(R19_q), .in20(R20_q), .in21(R21_q), .in22(R22_q),
    .in23(R23_q), .in24(R24_q), .in25(R25_q), .in26(R26_q), .in27(R27_q), .in28(R28_q), .in29(R29_q),
    .in30(R30_q), .in31(R31_q), .out(BusA), .sel(RA_Rs));  // open: en
  Multiplexer #(.select(5), .width(32)) multiplexer_2 (
    .in0(R0_q), .in1(R1_q), .in2(R2_q), .in3(R3_q), .in4(R4_q), .in5(a1), .in6(R6_q), .in7(R7_q), .in8(R8_q),
    .in9(R9_q), .in10(R10_q), .in11(R11_q), .in12(R12_q), .in13(R13_q), .in14(R14_q), .in15(R15_q),
    .in16(R16_q), .in17(R17_q), .in18(R18_q), .in19(R19_q), .in20(R20_q), .in21(R21_q), .in22(R22_q),
    .in23(R23_q), .in24(R24_q), .in25(R25_q), .in26(R26_q), .in27(R27_q), .in28(R28_q), .in29(R29_q),
    .in30(R30_q), .in31(R31_q), .out(BusB), .sel(RB_Rt));  // open: en
endmodule

module main (
  input  [23:0] \memory_değerlerini_okumak_için_kullanıyoruz ,
  input  in_2,
  output [4:0] out_3,
  output [4:0] out_4,
  output [4:0] out_5,
  output [4:0] out_6,
  output [5:0] opcode
);

  wire alu_1_zero_flag, clock_1_out, ex_1_alusrc, ex_1_beq_bne, hazarddetection_1_stall, maincontrol_1_j,
       maincontrol_1_regdst, mem_1_memrd, mem_1_memwr, mem_1_wb_regwr, mem_1_wbdata, not_1_out, or_1_out,
       pccontrol_1_kill1, pccontrol_1_kill2, WB_q;
  wire [1:0] hazarddetection_1_forwarda, hazarddetection_1_forwardb, pccontrol_1_pcsrc;
  wire [3:0] ex_1_aluop, ex_1_mem;
  wire [4:0] multiplexer_3_out, Rd3_q, Rd4_q, sa_q;
  wire [9:0] maincontrol_1_exinput, multiplexer_4_out;
  wire [15:0] inst_q;
  wire [31:0] A_q, adder_1_out, alu_1_alu_out, B_q, bit_extender_1_out, BTA_q, D_q, Data_q, Imm_q,
       multiplexer_1_out, multiplexer_2_out, multiplexer_5_out, multiplexer_6_out, multiplexer_7_out,
       multiplexer_8_out, NPC_q, part_1_branch_target_address, PC_q, R_q, ram_1_data, registers_1_a1,
       registers_1_busa, registers_1_busb, rom_1_data;

  Clock clock_1 (.out(clock_1_out));
  Multiplexer #(.select(2), .width(32)) multiplexer_1 (
    .in0(adder_1_out), .in1({opcode, out_3, out_5, inst_q[15:11], out_4, inst_q[5:0]}), .in2(BTA_q),
    .out(multiplexer_1_out), .sel(pccontrol_1_pcsrc));  // open: in3, en
  PCcontrol pccontrol_1 (
    .bne(ex_1_beq_bne), .zero(alu_1_zero_flag), .j(maincontrol_1_j), .PCsrc(pccontrol_1_pcsrc), .beq(in_2),
    .Kill1(pccontrol_1_kill1), .Kill2(pccontrol_1_kill2));
  Register #(.width(32)) PC (.D(multiplexer_1_out), .en(not_1_out), .Q(PC_q), .clk(clock_1_out));  // open: clr
  Adder #(.width(32)) adder_1 (.a(32'h4), .b(PC_q), .out(adder_1_out));  // open: cin, cout
  ROM #(.addrWidth(24), .dataWidth(32)) rom_1 (.addr(PC_q[25:2]), .data(rom_1_data));  // open: sel
  Multiplexer #(.width(32)) multiplexer_2 (
    .in0(rom_1_data), .in1({32{1'b0}}), .out(multiplexer_2_out), .sel(pccontrol_1_kill1));  // open: en
  not not_1 (not_1_out, hazarddetection_1_stall);
  Register #(.width(32)) NPC (.D(adder_1_out), .en(not_1_out), .Q(NPC_q), .clk(clock_1_out));  // open: clr
  Register #(.width(32)) inst (
    .D(multiplexer_2_out), .en(not_1_out), .Q({opcode, out_3, out_5, inst_q[15:11], out_4, inst_q[5:0]}),
    .clk(clock_1_out));  // open: clr
  Hex_Digit_Display hex_digit_display_1 (.value(registers_1_a1[3:0]));  // open: dp
  assign bit_extender_1_out = {{16{inst_q[15]}}, {inst_q[15:11], out_4, inst_q[5:0]}};  // Bit_Extender bit_extender_1
  Multiplexer #(.width(5)) multiplexer_3 (
    .in0(out_5), .in1(inst_q[15:11]), .out(multiplexer_3_out), .sel(maincontrol_1_regdst));  // open: en
  MainControl maincontrol_1 (
    .func(inst_q[5:0]), .OpCode(opcode), .EXinput(maincontrol_1_exinput), .regDst(maincontrol_1_regdst),
    .J(maincontrol_1_j));
  circuit part_1 (
    .next_pc_address(NPC_q), .imm32(bit_extender_1_out), .Branch_Target_Address(part_1_branch_target_address));
  Registers registers_1 (
    .RW(Rd4_q), .RB_Rt(out_5), .BusA(registers_1_busa), .RA_Rs(out_3), .BusB(registers_1_busb),
    .BusW(Data_q), .RegWr(WB_q), .clock(clock_1_out), .a1(registers_1_a1));
  HazardDetection hazarddetection_1 (
    .Rt(out_5), .Rs(out_3), .MEMread(ex_1_mem[3]), .EX_RegWR(ex_1_mem[0]), .MEM_RegWR(mem_1_wb_regwr),
    .WB_RegWR(WB_q), .Rd2(out_6), .Rd3(Rd3_q), .Rd4(Rd4_q), .ForwardA(hazarddetection_1_forwarda),
    .ForwardB(hazarddetection_1_forwardb), .Stall(hazarddetection_1_stall));
  or or_1 (or_1_out, hazarddetection_1_stall, pccontrol_1_kill2);
  Multiplexer #(.width(10)) multiplexer_4 (
    .in0(maincontrol_1_exinput), .in1({10{1'b0}}), .out(multiplexer_4_out), .sel(or_1_out));  // open: en
  Multiplexer #(.select(2), .width(32)) multiplexer_5 (
    .in0(registers_1_busa), .in1(Data_q), .in2(multiplexer_8_out), .in3(alu_1_alu_out),
    .out(multiplexer_5_out), .sel(hazarddetection_1_forwarda));  // open: en
  Multiplexer #(.select(2), .width(32)) multiplexer_6 (
    .in0(registers_1_busb), .in1(Data_q), .in2(multiplexer_8_out), .in3(alu_1_alu_out),
    .out(multiplexer_6_out), .sel(hazarddetection_1_forwardb));  // open: en
  Register #(.width(32)) BTA (.D(part_1_branch_target_address), .Q(BTA_q), .clk(clock_1_out));  // open: en, clr
  Register #(.width(32)) Imm (.D(bit_extender_1_out), .Q(Imm_q), .clk(clock_1_out));  // open: en, clr
  Register #(.width(32)) A (.D(multiplexer_5_out), .Q(A_q), .clk(clock_1_out));  // open: en, clr
  Register #(.width(32)) B (.D(multiplexer_6_out), .Q(B_q), .clk(clock_1_out));  // open: en, clr
  Register #(.width(5)) Rd2 (.D(multiplexer_3_out), .Q(out_6), .clk(clock_1_out));  // open: en, clr
  Register #(.width(5)) sa (.D(out_4), .Q(sa_q), .clk(clock_1_out));  // open: en, clr
  EX ex_1 (
    .\input (multiplexer_4_out), .clock(clock_1_out), .BEQ_BNE(ex_1_beq_bne), .MEM(ex_1_mem),
    .ALUSrc(ex_1_alusrc), .ALUop(ex_1_aluop));
  Multiplexer #(.width(32)) multiplexer_7 (
    .in0(B_q), .in1(Imm_q), .out(multiplexer_7_out), .sel(ex_1_alusrc));  // open: en
  ALU alu_1 (
    .ALU_OUT(alu_1_alu_out), .zero_flag(alu_1_zero_flag), .A(A_q), .B(multiplexer_7_out), .in_3(ex_1_aluop),
    .shift_amount(sa_q));
  Register #(.width(32)) R (.D(alu_1_alu_out), .Q(R_q), .clk(clock_1_out));  // open: en, clr
  Register #(.width(32)) D (.D(B_q), .Q(D_q), .clk(clock_1_out));  // open: en, clr
  Register #(.width(5)) Rd3 (.D(out_6), .Q(Rd3_q), .clk(clock_1_out));  // open: en, clr
  MEM mem_1 (
    .in(ex_1_mem), .MEMrd(mem_1_memrd), .MEMwr(mem_1_memwr), .WBdata(mem_1_wbdata),
    .WB_regWR(mem_1_wb_regwr), .clk(clock_1_out));
  RAM #(.addrWidth(24), .dataWidth(32), .bus("separate")) ram_1 (
    .addr(R_q[23:0]), .din(D_q), .data(ram_1_data), .str(mem_1_memwr), .clk(clock_1_out), .ld(mem_1_memrd));  // open: sel, clr
  Multiplexer #(.width(32)) multiplexer_8 (
    .in0(R_q), .in1(ram_1_data), .out(multiplexer_8_out), .sel(mem_1_wbdata));  // open: en
  Register #(.width(32)) Data (.D(multiplexer_8_out), .Q(Data_q), .clk(clock_1_out));  // open: en, clr
  Register #(.width(5)) Rd4 (.D(Rd3_q), .Q(Rd4_q), .clk(clock_1_out));  // open: en, clr
  Register #(.width(1)) WB (.D(mem_1_wb_regwr), .Q(WB_q), .clk(clock_1_out));  // open: en, clr

  // Notes on the sheet:
  //   contents of rom_1 (hex, n*v repeats v):
  //   2005000a 6820 6daa0000 14a5820 8dab0000 20a5ffff 21ad0001 14a0fffa 8*0 12 13 14 15 16 17 18 99 566
  //   77545 7577 1140 47776 1354 427 12440
  //   imm
  //   opcode
  //   func
  //   rs
  //   rt
  //   rd
  //   sa
  //   $a1
  //   ForwardB
  //   ForwardA
  //   MEMrd
  //   RegWB
  //   read
endmodule

module circuit (
  input  [31:0] next_pc_address,
  input  [31:0] imm32,
  output [31:0] Branch_Target_Address
);

  wire [31:0] shifter_1_out;

  Shifter #(.width(32)) shifter_1 (.in(imm32), .\dist (5'b00010), .out(shifter_1_out));
  Adder #(.width(32)) adder_1 (.a(next_pc_address), .b(shifter_1_out), .out(Branch_Target_Address));  // open: cin, cout
endmodule

module MEM (
  input  [3:0] in,
  input  clk,
  output MEMrd,
  output MEMwr,
  output WBdata,
  output WB_regWR
);

  Register #(.width(1)) u_Memrd (.D(in[3]), .Q(MEMrd), .clk(clk));  // open: en, clr
  Register #(.width(1)) u_MemWr (.D(in[2]), .Q(MEMwr), .clk(clk));  // open: en, clr
  Register #(.width(1)) u_WBdata (.D(in[1]), .Q(WBdata), .clk(clk));  // open: en, clr
  Register #(.width(1)) WB (.D(in[0]), .Q(WB_regWR), .clk(clk));  // open: en, clr
endmodule

module EX (
  input  [9:0] \input ,
  input  clock,
  output BEQ_BNE,
  output [3:0] MEM,
  output ALUSrc,
  output [3:0] ALUop
);

  Register #(.width(1)) register_1 (.D(\input [0]), .Q(BEQ_BNE), .clk(clock));  // open: en, clr
  Register #(.width(4)) register_2 (.D(\input [4:1]), .Q(MEM), .clk(clock));  // open: en, clr
  Register #(.width(1)) register_3 (.D(\input [5]), .Q(ALUSrc), .clk(clock));  // open: en, clr
  Register #(.width(4)) register_4 (.D(\input [9:6]), .Q(ALUop), .clk(clock));  // open: en, clr
endmodule

module MainControl (
  input  [5:0] func,
  input  [5:0] OpCode,
  output J,
  output regDst,
  output [9:0] EXinput
);

  wire and_1_out;
  wire [11:0] rom_1_data, rom_2_data;

  and and_1 (and_1_out, ~OpCode[0], ~OpCode[1], ~OpCode[2], ~OpCode[3], ~OpCode[4], ~OpCode[5]);  // AND_Gate
  ROM #(.addrWidth(6), .dataWidth(12)) rom_1 (.addr(func), .data(rom_1_data));  // open: sel
  ROM #(.addrWidth(6), .dataWidth(12)) rom_2 (.addr(OpCode), .data(rom_2_data));  // open: sel
  Multiplexer #(.width(12)) multiplexer_1 (
    .in0(rom_2_data), .in1(rom_1_data), .out({EXinput[9:1], regDst, EXinput[0], J}), .sel(and_1_out));  // open: en

  // Notes on the sheet:
  //   contents of rom_1 (hex, n*v repeats v):
  //   70c 0 80c 28*0 40c 40c 0 50c 0 c 10c 20c
  //   contents of rom_2 (hex, n*v repeats v):
  //   5*0 502 0 0 488 18*0 4d8 7*0 4a0
endmodule

module PCcontrol (
  input  bne,
  input  zero,
  input  j,
  input  beq,
  output [1:0] PCsrc,
  output Kill1,
  output Kill2
);

  wire and_1_out, and_2_out, and_3_out, and_4_out, and_5_out, and_6_out, and_7_out, and_8_out, JUMP_out,
       or_1_out, or_2_out;

  and and_1 (and_1_out, ~bne, zero, ~j, beq);  // AND_Gate
  and and_2 (and_2_out, bne, ~zero, ~j, ~beq);  // AND_Gate
  and and_3 (and_3_out, ~bne, zero, j, ~beq);  // AND_Gate
  and and_4 (and_4_out, ~bne, ~zero, j, ~beq);  // AND_Gate
  and and_5 (and_5_out, ~bne, zero, ~j, ~beq);  // AND_Gate
  and and_6 (and_6_out, ~bne, ~zero, ~j, ~beq);  // AND_Gate
  and and_7 (and_7_out, bne, ~zero);  // AND_Gate
  and and_8 (and_8_out, beq, zero);
  or or_1 (or_1_out, and_7_out, and_8_out);
  or Br (Kill2, and_1_out, and_2_out);
  or JUMP (JUMP_out, and_3_out, and_4_out);
  or or_2 (or_2_out, and_5_out, and_6_out);
  // AND_Gate and_9 has open pins: in0=j, in1=or_1_out, out=open
  Priority_Encoder #(.select(2)) priority_encoder_1 (
    .in0(or_2_out), .in1(JUMP_out), .in2(Kill2), .out(PCsrc));  // open: in3, gs, en_out, en_in
  or or_3 (Kill1, Kill2, JUMP_out);
endmodule

module HazardDetection (
  input  MEMread,
  input  [4:0] Rt,
  input  [4:0] Rs,
  input  EX_RegWR,
  input  MEM_RegWR,
  input  WB_RegWR,
  input  [4:0] Rd2,
  input  [4:0] Rd3,
  input  [4:0] Rd4,
  output [1:0] ForwardA,
  output Stall,
  output [1:0] ForwardB
);

  wire and_1_out, and_2_out, and_3_out, and_4_out, and_5_out, and_6_out, and_7_out, and_8_out,
       comparator_1_eq, comparator_2_eq, comparator_3_eq, comparator_4_eq, comparator_5_eq, comparator_6_eq,
       comparator_7_eq, comparator_8_eq, comparator_9_eq, comparator_10_eq, not_1_out, not_2_out, or_1_out;

  not not_1 (not_1_out, comparator_1_eq);
  Comparator #(.width(5)) comparator_1 (.a(Rs), .b({5{1'b0}}), .eq(comparator_1_eq));  // open: gt, lt
  Comparator #(.width(5)) comparator_2 (.a(Rs), .b(Rd2), .eq(comparator_2_eq));  // open: gt, lt
  Comparator #(.width(5)) comparator_3 (.a(Rs), .b(Rd3), .eq(comparator_3_eq));  // open: gt, lt
  Comparator #(.width(5)) comparator_4 (.a(Rs), .b(Rd4), .eq(comparator_4_eq));  // open: gt, lt
  and and_1 (and_1_out, not_1_out, comparator_2_eq, EX_RegWR);
  and and_2 (and_2_out, not_1_out, comparator_3_eq, MEM_RegWR);
  and and_3 (and_3_out, not_1_out, comparator_4_eq, WB_RegWR);
  and and_4 (and_4_out, ~and_1_out, ~and_2_out, ~and_3_out);  // AND_Gate
  Comparator #(.width(5)) comparator_5 (.a(Rt), .b({5{1'b0}}), .eq(comparator_5_eq));  // open: gt, lt
  not not_2 (not_2_out, comparator_5_eq);
  Comparator #(.width(5)) comparator_6 (.a(Rt), .b(Rd2), .eq(comparator_6_eq));  // open: gt, lt
  Comparator #(.width(5)) comparator_7 (.a(Rt), .b(Rd3), .eq(comparator_7_eq));  // open: gt, lt
  Comparator #(.width(5)) comparator_8 (.a(Rt), .b(Rd4), .eq(comparator_8_eq));  // open: gt, lt
  Priority_Encoder #(.select(2)) priority_encoder_1 (
    .in0(and_4_out), .in1(and_3_out), .in2(and_2_out), .in3(and_1_out), .out(ForwardA));  // open: gs, en_out, en_in
  and and_5 (and_5_out, not_2_out, comparator_6_eq, EX_RegWR);
  and and_6 (and_6_out, not_2_out, comparator_7_eq, MEM_RegWR);
  and and_7 (and_7_out, not_2_out, comparator_8_eq, WB_RegWR);
  Comparator #(.width(2)) comparator_9 (.a(ForwardA), .b(2'b11), .eq(comparator_9_eq));  // open: gt, lt
  and and_8 (and_8_out, ~and_5_out, ~and_6_out, ~and_7_out);  // AND_Gate
  Priority_Encoder #(.select(2)) priority_encoder_2 (
    .in0(and_8_out), .in1(and_7_out), .in2(and_6_out), .in3(and_5_out), .out(ForwardB));  // open: gs, en_out, en_in
  Comparator #(.width(2)) comparator_10 (.a(ForwardB), .b(2'b11), .eq(comparator_10_eq));  // open: gt, lt
  or or_1 (or_1_out, comparator_9_eq, comparator_10_eq);
  and and_9 (Stall, MEMread, or_1_out);

  // Notes on the sheet:
  //   Rs
endmodule
