// Logisim project CPUwithRegisters.circ as structural Verilog: 3 circuits, main circuit main
module ALU (
  input  [31:0] A,
  input  [31:0] B,
  input  [3:0] in_3,
  output [31:0] ALU_OUT,
  output zero_flag
);

  wire [31:0] adder_1_out, and_1_out, negator_1_out, not_1_out, or_1_out, shifter_1_out, shifter_2_out,
       subtractor_1_out, xor_1_out;

  assign and_1_out = B & A;  // AND_Gate and_1, 32 bits wide
  assign or_1_out = B | A;  // OR_Gate or_1, 32 bits wide
  assign xor_1_out = B ^ A;  // XOR_Gate xor_1, 32 bits wide
  assign not_1_out = ~A;  // NOT_Gate not_1, 32 bits wide
  Adder #(.width(32)) adder_1 (.a(A), .b(B), .out(adder_1_out));  // open: cin, cout
  Subtractor #(.width(32)) subtractor_1 (.a(A), .b(B), .out(subtractor_1_out));  // open: bin, bout
  Negator #(.width(32)) negator_1 (.in(A), .out(negator_1_out));
  Shifter #(.width(32)) shifter_1 (.in(A), .\dist (B[4:0]), .out(shifter_1_out));
  Shifter #(.width(32), .shift("lr")) shifter_2 (.in(A), .\dist (B[4:0]), .out(shifter_2_out));
  Multiplexer #(.select(4), .width(32)) multiplexer_1 (
    .in0(and_1_out), .in1(or_1_out), .in2(xor_1_out), .in3(not_1_out), .in4(adder_1_out),
    .in5(subtractor_1_out), .in6(negator_1_out), .in7(shifter_1_out), .in8(shifter_2_out), .out(ALU_OUT),
    .sel(in_3));  // open: in9, in10, in11, in12, in13, in14, in15, en
  Comparator #(.width(32)) comparator_1 (.a(ALU_OUT), .b({32{1'b0}}), .eq(zero_flag));  // open: gt, lt

  // Notes on the sheet:
  //   A+B
  //   A-B
  //   -A
  //   logic left
  //   logic right
endmodule

module Registers (
  input  [31:0] BusW,
  input  RegWr,
  input  [4:0] RW,
  input  [4:0] RA_Rs,
  input  [4:0] RB_Rt,
  output [31:0] BusA,
  output [31:0] BusB
);

  wire clock_1_out, demultiplexer_1_out0, demultiplexer_1_out1, demultiplexer_1_out2, demultiplexer_1_out3,
       demultiplexer_1_out4, demultiplexer_1_out5, demultiplexer_1_out6, demultiplexer_1_out7,
       demultiplexer_1_out8, demultiplexer_1_out9, demultiplexer_1_out10, demultiplexer_1_out11,
       demultiplexer_1_out12, demultiplexer_1_out13, demultiplexer_1_out14, demultiplexer_1_out15,
       demultiplexer_1_out16, demultiplexer_1_out17, demultiplexer_1_out18, demultiplexer_1_out19,
       demultiplexer_1_out20, demultiplexer_1_out21, demultiplexer_1_out22, demultiplexer_1_out23,
       demultiplexer_1_out24, demultiplexer_1_out25, demultiplexer_1_out26, demultiplexer_1_out27,
       demultiplexer_1_out28, demultiplexer_1_out29, demultiplexer_1_out30, demultiplexer_1_out31;
  wire [31:0] R0_q, R1_q, R2_q, R4_q, R6_q, R8_q, R10_q, R12_q, R14_q, R16_q, R18_q, R20_q, R22_q, R24_q,
       R25_q, R26_q, R27_q, R28_q, R29_2_q, R29_3_q, R29_4_q, R29_5_q, R29_6_q, R29_7_q, R29_8_q, R29_9_q,
       R29_10_q, R29_11_q, R29_12_q, R29_q, R30_q, R31_q;

  Clock clock_1 (.out(clock_1_out));
  Demultiplexer #(.select(5)) demultiplexer_1 (
    .out0(demultiplexer_1_out0), .out1(demultiplexer_1_out1), .out2(demultiplexer_1_out2),
    .out3(demultiplexer_1_out3), .out4(demultiplexer_1_out4), .out5(demultiplexer_1_out5),
    .out6(demultiplexer_1_out6), .out7(demultiplexer_1_out7), .out8(demultiplexer_1_out8),
    .out9(demultiplexer_1_out9), .out10(demultiplexer_1_out10), .out11(demultiplexer_1_out11),
    .out12(demultiplexer_1_out12), .out13(demultiplexer_1_out13), .out14(demultiplexer_1_out14),
    .out15(demultiplexer_1_out15), .out16(demultiplexer_1_out16), .out17(demultiplexer_1_out17),
    .out18(demultiplexer_1_out18), .out19(demultiplexer_1_out19), .out20(demultiplexer_1_out20),
    .out21(demultiplexer_1_out21), .out22(demultiplexer_1_out22), .out23(demultiplexer_1_out23),
    .out24(demultiplexer_1_out24), .out25(demultiplexer_1_out25), .out26(demultiplexer_1_out26),
    .out27(demultiplexer_1_out27), .out28(demultiplexer_1_out28), .out29(demultiplexer_1_out29),
    .out30(demultiplexer_1_out30), .out31(demultiplexer_1_out31), .in(clock_1_out), .sel(RW), .en(RegWr));
  Register #(.width(32)) R31 (.D(BusW), .Q(R31_q), .clk(demultiplexer_1_out31));  // open: en, clr
  Register #(.width(32)) R29 (.D(BusW), .Q(R29_q), .clk(demultiplexer_1_out29));  // open: en, clr
  Register #(.width(32)) R27 (.D(BusW), .Q(R27_q), .clk(demultiplexer_1_out27));  // open: en, clr
  Register #(.width(32)) R25 (.D(BusW), .Q(R25_q), .clk(demultiplexer_1_out25));  // open: en, clr
  Register #(.width(32)) R29_2 (.D(BusW), .Q(R29_2_q), .clk(demultiplexer_1_out23));  // open: en, clr
  Register #(.width(32)) R29_3 (.D(BusW), .Q(R29_3_q), .clk(demultiplexer_1_out21));  // open: en, clr
  Register #(.width(32)) R29_4 (.D(BusW), .Q(R29_4_q), .clk(demultiplexer_1_out19));  // open: en, clr
  Register #(.width(32)) R29_5 (.D(BusW), .Q(R29_5_q), .clk(demultiplexer_1_out17));  // open: en, clr
  Register #(.width(32)) R29_6 (.D(BusW), .Q(R29_6_q), .clk(demultiplexer_1_out15));  // open: en, clr
  Register #(.width(32)) R29_7 (.D(BusW), .Q(R29_7_q), .clk(demultiplexer_1_out13));  // open: en, clr
  Register #(.width(32)) R29_8 (.D(BusW), .Q(R29_8_q), .clk(demultiplexer_1_out11));  // open: en, clr
  Register #(.width(32)) R29_9 (.D(BusW), .Q(R29_9_q), .clk(demultiplexer_1_out9));  // open: en, clr
  Register #(.width(32)) R29_10 (.D(BusW), .Q(R29_10_q), .clk(demultiplexer_1_out7));  // open: en, clr
  Register #(.width(32)) R29_11 (.D(BusW), .Q(R29_11_q), .clk(demultiplexer_1_out5));  // open: en, clr
  Register #(.width(32)) R29_12 (.D(BusW), .Q(R29_12_q), .clk(demultiplexer_1_out3));  // open: en, clr
  Register #(.width(32)) R1 (.D(BusW), .Q(R1_q), .clk(demultiplexer_1_out1));  // open: en, clr
  Register #(.width(32)) R30 (.D(BusW), .Q(R30_q), .clk(demultiplexer_1_out30));  // open: en, clr
  Register #(.width(32)) R28 (.D(BusW), .Q(R28_q), .clk(demultiplexer_1_out28));  // open: en, clr
  Register #(.width(32)) R26 (.D(BusW), .Q(R26_q), .clk(demultiplexer_1_out26));  // open: en, clr
  Register #(.width(32)) R24 (.D(BusW), .Q(R24_q), .clk(demultiplexer_1_out24));  // open: en, clr
  Register #(.width(32)) R22 (.D(BusW), .Q(R22_q), .clk(demultiplexer_1_out22));  // open: en, clr
  Register #(.width(32)) R20 (.D(BusW), .Q(R20_q), .clk(demultiplexer_1_out20));  // open: en, clr
  Register #(.width(32)) R18 (.D(BusW), .Q(R18_q), .clk(demultiplexer_1_out18));  // open: en, clr
  Register #(.width(32)) R16 (.D(BusW), .Q(R16_q), .clk(demultiplexer_1_out16));  // open: en, clr
  Register #(.width(32)) R14 (.D(BusW), .Q(R14_q), .clk(demultiplexer_1_out14));  // open: en, clr
  Register #(.width(32)) R12 (.D(BusW), .Q(R12_q), .clk(demultiplexer_1_out12));  // open: en, clr
  Register #(.width(32)) R10 (.D(BusW), .Q(R10_q), .clk(demultiplexer_1_out10));  // open: en, clr
  Register #(.width(32)) R8 (.D(BusW), .Q(R8_q), .clk(demultiplexer_1_out8));  // open: en, clr
  Register #(.width(32)) R6 (.D(BusW), .Q(R6_q), .clk(demultiplexer_1_out6));  // open: en, clr
  Register #(.width(32)) R4 (.D(BusW), .Q(R4_q), .clk(demultiplexer_1_out4));  // open: en, clr
  Register #(.width(32)) R2 (.D(BusW), .Q(R2_q), .clk(demultiplexer_1_out2));  // open: en, clr
  Register #(.width(32)) R0 (.D({32{1'b0}}), .Q(R0_q), .clk(demultiplexer_1_out0));  // open: en, clr
  Multiplexer #(.select(5), .width(32)) multiplexer_1 (
    .in0(R0_q), .in1(R1_q), .in2(R2_q), .in3(R29_12_q), .in4(R4_q), .in5(R29_11_q), .in6(R6_q),
    .in7(R29_10_q), .in8(R8_q), .in9(R29_9_q), .in10(R10_q), .in11(R29_8_q), .in12(R12_q), .in13(R29_7_q),
    .in14(R14_q), .in15(R29_6_q), .in16(R16_q), .in17(R29_5_q), .in18(R18_q), .in19(R29_4_q), .in20(R20_q),
    .in21(R29_3_q), .in22(R22_q), .in23(R29_2_q), .in24(R24_q), .in25(R25_q), .in26(R26_q), .in27(R27_q),
    .in28(R28_q), .in29(R29_q), .in30(R30_q), .in31(R31_q), .out(BusA), .sel(RA_Rs));  // open: en
  Multiplexer #(.select(5), .width(32)) multiplexer_2 (
    .in0(R0_q), .in1(R1_q), .in2(R2_q), .in3(R29_12_q), .in4(R4_q), .in5(R29_11_q), .in6(R6_q),
    .in7(R29_10_q), .in8(R8_q), .in9(R29_9_q), .in10(R10_q), .in11(R29_8_q), .in12(R12_q), .in13(R29_7_q),
    .in14(R14_q), .in15(R29_6_q), .in16(R16_q), .in17(R29_5_q), .in18(R18_q), .in19(R29_4_q), .in20(R20_q),
    .in21(R29_3_q), .in22(R22_q), .in23(R29_2_q), .in24(R24_q), .in25(R25_q), .in26(R26_q), .in27(R27_q),
    .in28(R28_q), .in29(R29_q), .in30(R30_q), .in31(R31_q), .out(BusB), .sel(RB_Rt));  // open: en

  // Notes on the sheet:
  //   RegWr girişini gözden geçir. Doğru yere mi bağladım bilmiyorum????
endmodule

module main (
);

  ALU alu_1 ();  // open: ALU_OUT, zero_flag, A, B, in_3
  Registers registers_1 ();  // open: RW, RB_Rt, BusA, RA_Rs, BusB, BusW, RegWr
endmodule
